# Fritzing sketch ledRGB (saved by Fritzing 0.9.2b)
breadboards: 1

parts:
  Part1 = Arduino Uno (Rev3)
  R2 = Resistor [tolerance=±5% resistance=270 package=THT]
  LED2 = RGB LED (com. anode, rbg) [package="5 mm [THT]"]
  R3 = Resistor [tolerance=±5% resistance=270 package=THT]
  R4 = Resistor [tolerance=±5% resistance=270 package=THT]

nets:
  N1: Part1.D10_PWM/SS, R3.Pin_1
  N2: Part1.D11_PWM/MOSI, R2.Pin_1
  N3: R2.Pin_0, LED2.red_cathode
  N4: LED2.blue_cathode, R3.Pin_0
  N5: LED2.green_cathode, R4.Pin_0
