# Fritzing sketch led_pwm (saved by Fritzing 0.9.2b)
breadboards: 1

parts:
  Part1 = Arduino Uno (Rev3)
  R2 = Resistor [tolerance=±5% resistance=220 package=THT]
  LED1 = LED - 3mm [color="Red (633nm)" package="3 mm [THT]"]

nets:
  N1: Part1.D3_PWM, LED1.anode
  N2: Part1.GND, R2.Pin_1
  N3: R2.Pin_0, LED1.cathode
