# Fritzing sketch mosfet_ledjes (saved by Fritzing 0.9.2b)
breadboards: 1

parts:
  Part1 = Arduino Uno (Rev3)
  Q1 = Basic FET P-Channel [package="TO220 [THT]"]
  LED1 = smd LED [color="Red (633nm)" package="0805 [SMD]"]
  VCC1 = Battery

nets:
  N1: Part1.D2, Q1.gate
  N2: Part1.GND, Q1.source, LED1.cathode
  N3: Q1.drain, VCC1.+

notes:
  het is crappy dat de ledjes aan de grond zitten maarjah mijn ledjesslinger is zo helaas pindakaas
  Tzijn ook 3 batterijen -> 4,5V
