# Fritzing sketch servo_pwm (saved by Fritzing 0.9.2b)
breadboards: 1

parts:
  Part1 = Arduino Uno (Rev3)
  J1 = Basic Servo
  C1 = Capacitor Polarized [package=cpol-radial-100uf-25v]

nets:
  N1: Part1.D3_PWM, J1.pulse
  5V: Part1.5V, J1.vcc, C1.-
  GND: Part1.GND, J1.gnd, C1.+
