# Fritzing sketch drawing (saved by Fritzing 0.9.2b)
breadboards: 1

parts:
  Part1 = Arduino Uno (Rev3)
  DI1 = 7-Segment LED Display [package=THT]  # not connected
  R1 = Resistor [tolerance=±5% resistance=220 package="2010 [SMD]"]
  R2 = Resistor [tolerance=±5% resistance=220 package="2010 [SMD]"]
  R3 = Resistor [tolerance=±5% resistance=220 package="2010 [SMD]"]
  R4 = Resistor [tolerance=±5% resistance=220 package="2010 [SMD]"]
  R5 = Resistor [tolerance=±5% resistance=220 package="2010 [SMD]"]
  R6 = Resistor [tolerance=±5% resistance=220 package="2010 [SMD]"]
  R7 = Resistor [tolerance=±5% resistance=220 package="2010 [SMD]"]
  R8 = Resistor [tolerance=±5% resistance=220 package="2010 [SMD]"]

nets:
  N1: Part1.D8, R7.Pin_1
  N2: Part1.D9_PWM, R8.Pin_1
  N3: Part1.D2, R1.Pin_0
  N4: Part1.D3_PWM, R2.Pin_0
  N5: Part1.D4, R6.Pin_0
  N6: Part1.D5_PWM, R5.Pin_0
  N7: Part1.D6_PWM, R3.Pin_1
  N8: Part1.D7, R4.Pin_1
