# Fritzing sketch Piezo-input (saved by Fritzing 0.9.2b)
breadboards: 1

parts:
  Part1 = Arduino Uno (Rev3)
  R2 = Resistor [tolerance=±5% resistance=1M package=THT]
  J1 = Piezo Speaker

nets:
  N1: Part1.A0, R2.Pin_1, J1.pin2
  N2: Part1.5V, R2.Pin_0
  N3: Part1.GND, J1.pin1
