# Fritzing sketch Tiltsensor (saved by Fritzing 0.9.2b)
breadboards: 1

parts:
  Part1 = Arduino Uno (Rev3)
  R2 = Resistor [tolerance=±5% resistance=10k package=THT]
  S1 = Tilt Switch [package=THT]

nets:
  N1: Part1.D6_PWM, R2.Pin_1, S1.Pin_2
  N2: Part1.5V, R2.Pin_0
  N3: Part1.GND, S1.Pin_1
