# Fritzing sketch druksensor (saved by Fritzing 0.9.2b)
breadboards: 1

parts:
  Part1 = Arduino Uno (Rev3)
  R2 = Resistor [tolerance=±5% resistance=10k package=THT]
  J1 = Basic Force Sensing Resistor (FSR) [package=THT]

nets:
  N1: Part1.A0, R2.Pin_1, J1.pin_1
  N2: Part1.5V, R2.Pin_0
  N3: Part1.GND, J1.pin_0
