# Fritzing sketch knop (saved by Fritzing 0.9.2b)
breadboards: 1

parts:
  Part1 = Arduino Uno (Rev3)
  R2 = Resistor [tolerance=±5% resistance=10k package=THT]
  S1 = Momentary Switch [package=ksa_sealed_tac_switch]

nets:
  N1: Part1.D2, R2.Pin_1, S1.3
  N2: Part1.5V, R2.Pin_0
  N3: Part1.GND, S1.1
