# Fritzing sketch lichtsensor (saved by Fritzing 0.9.2b)
breadboards: 1

parts:
  Part1 = Arduino Uno (Rev3)
  R2 = Resistor [tolerance=±5% resistance=10k package=THT]
  R1 = PHOTOCELL [package=photocell-kit]

nets:
  N1: Part1.A0, R2.Pin_1, R1.P$1
  N2: Part1.5V, R2.Pin_0
  N3: Part1.GND, R1.P$2
